# Fritzing sketch Smart_Piggy_Bank (saved by Fritzing 0.9.3b)
breadboards: 1

parts:
  Part1 = Arduino Uno (Rev3)
  e-radionica1 = TCS230 Color Sensor [part_number=101209]
  LCD1 = LCD screen
  R1 = Trimmer Potentiometer [maximum_resistance=10kΩ package=THT]
  M1 = fc-51 [package=THT]

nets (from the breadboard view):
  N1: Part1.A0, M1.pin1
  N2: Part1.D8, LCD1.DB5
  N3: Part1.D9_PWM, LCD1.DB6
  N4: Part1.D10_PWM/SS, LCD1.DB7
  N5: Part1.D11_PWM/MOSI, e-radionica1.S2
  N6: Part1.D12/MISO, e-radionica1.S3
  5V: Part1.D13/SCK, Part1.5V, e-radionica1.Out, e-radionica1.Vcc, LCD1.VDD, LCD1.LED+, R1.leg1, M1.pin3
  N7: Part1.D2, e-radionica1.S0
  N8: Part1.D3_PWM, e-radionica1.S1
  N9: Part1.D5_PWM, LCD1.RS
  N10: Part1.D6_PWM, LCD1.E
  N11: Part1.D7, LCD1.DB4
  GND: Part1.GND, e-radionica1.Gnd, LCD1.VSS, LCD1.R/W, LCD1.LED-, R1.leg2, M1.pin2
  N12: LCD1.V0, R1.wiper

custom parts:
  TCS230 Color Sensor: TCS230
